# Fritzing sketch 面包板接线图 (saved by Fritzing 0.9.2b)
breadboards: 1

parts:
  元件1 = Arduino Uno (Rev3)
  LED1 = LED - 5mm [color="Red (633nm)" package="5 mm [THT]"]
  R1 = Resistor [tolerance=±5% resistance=220 package=THT]
  R2 = Resistor [tolerance=±5% resistance=220 package=THT]
  LED2 = LED - 5mm [color="Red (633nm)" package="5 mm [THT]"]
  R3 = Resistor [tolerance=±5% resistance=220 package=THT]
  LED3 = LED - 5mm [color="Red (633nm)" package="5 mm [THT]"]
  R4 = Resistor [tolerance=±5% resistance=220 package=THT]
  LED4 = LED - 5mm [color="Red (633nm)" package="5 mm [THT]"]
  R5 = Resistor [tolerance=±5% resistance=220 package=THT]
  LED5 = LED - 5mm [color="Red (633nm)" package="5 mm [THT]"]
  LED6 = LED - 5mm [color="Red (633nm)" package="5 mm [THT]"]
  LED7 = LED - 5mm [color="Red (633nm)" package="5 mm [THT]"]
  LED8 = LED - 5mm [color="Red (633nm)" package="5 mm [THT]"]
  R6 = Resistor [tolerance=±5% resistance=220 package=THT]
  R7 = Resistor [tolerance=±5% resistance=220 package=THT]
  R8 = Resistor [tolerance=±5% resistance=220 package=THT]

nets:
  N1: 元件1.D8, R7.Pin_0
  N2: 元件1.D9_PWM, R8.Pin_0
  N3: 元件1.D2, R1.Pin_0
  N4: 元件1.D3_PWM, R2.Pin_0
  N5: 元件1.D4, R3.Pin_0
  N6: 元件1.D5_PWM, R4.Pin_0
  N7: 元件1.D6_PWM, R5.Pin_0
  N8: 元件1.D7, R6.Pin_0
  N9: 元件1.5V, LED1.anode, LED2.anode, LED3.anode, LED4.anode, LED5.anode, LED6.anode, LED7.anode, LED8.anode
  N10: LED1.cathode, R1.Pin_1
  N11: R2.Pin_1, LED2.cathode
  N12: R3.Pin_1, LED3.cathode
  N13: R4.Pin_1, LED4.cathode
  N14: R5.Pin_1, LED5.cathode
  N15: LED6.cathode, R6.Pin_1
  N16: LED7.cathode, R7.Pin_1
  N17: LED8.cathode, R8.Pin_1

notes:
  22030716
